// Logisim project d16.circ as structural Verilog: 5 circuits, main circuit ALU
module main (
  output [15:0] out_1
);

  wire clock_1_out;
  wire [15:0] d16_1_rom_address, rom_1_data;

  ROM #(.addrWidth(16), .dataWidth(16)) rom_1 (.addr(d16_1_rom_address), .data(rom_1_data));  // open: sel
  d16 d16_1 (.Word_Out(out_1), .Word_In(rom_1_data), .ROM_Address(d16_1_rom_address), .Clock(clock_1_out));
  Clock clock_1 (.out(clock_1_out));
  TTY tty_1 (.data(out_1[6:0]), .clk(clock_1_out));  // open: we, clr

  // Notes on the sheet:
  //   contents of rom_1 (hex, n*v repeats v):
  //   df00 fffc de00 5f84 44e6 8080
endmodule

module d16 (
  input  [15:0] Word_In,
  input  Clock,
  output [15:0] ROM_Address,
  output [15:0] Word_Out
);

  wire eq, gt, im, ir, ou, pl, ps, re, rs;
  wire [2:0] r1, r2, rw;
  wire [3:0] op;
  wire [15:0] adder_1_out, alu_1_output, Immed_q, IR_q, multiplexer_1_out, multiplexer_2_out,
       registers_1_r1_out, registers_1_r2_out;

  Register #(.width(16)) Immed (.D(Word_In), .en(im), .Q(Immed_q), .clk(Clock));  // open: clr
  Register #(.width(16)) u_IR (.D(Word_In), .en(ir), .Q(IR_q), .clk(Clock));  // open: clr
  Multiplexer #(.width(16), .enable("false")) multiplexer_1 (
    .in0(Immed_q), .in1(alu_1_output), .out(multiplexer_1_out), .sel(rs));
  Control control_1 (
    .R2_Select(r2), .RW_Select(rw), .Op_Code(op), .Reg_Write(re), .IM_Load(im), .Reg_Select(rs),
    .PC_Load(pl), .R1___R2(eq), .IR_Load(ir), .R1___R2_2(gt), .Output(ou), .PC_Select(ps), .IR_Output(IR_q),
    .Clock(Clock), .R1_Select(r1));
  Register #(.width(16)) PC (.D(multiplexer_2_out), .en(pl), .Q(ROM_Address), .clk(Clock));  // open: clr
  Multiplexer #(.width(16), .enable("false")) multiplexer_2 (
    .in0(Immed_q), .in1(adder_1_out), .out(multiplexer_2_out), .sel(ps));
  Registers registers_1 (
    .Data_In(multiplexer_1_out), .R1_Out(registers_1_r1_out), .R2_Out(registers_1_r2_out), .Enable_Write(re),
    .R1_Select(r1), .R2_Select(r2), .Clock(Clock), .RW_Select(rw));
  ALU alu_1 (
    .Input_Register_1(registers_1_r1_out), .Input_Register_2(registers_1_r2_out), .R1___R2(gt),
    .R1___R2_2(eq), .Output(alu_1_output), .Operation_Code(op));
  Adder #(.width(16)) adder_1 (.a(ROM_Address), .b(16'h1), .out(adder_1_out));  // open: cin, cout
  assign Word_Out = ou ? registers_1_r1_out : 16'bz;  // Controlled_Buffer controlled_buffer_1
  Pull_Resistor pull_resistor_1 (.node(Word_Out));

  // Other names for the same wires on the sheet: clk = Clock
endmodule

module ALU (
  input  [15:0] Input_Register_1,
  input  [3:0] Operation_Code,
  input  [15:0] Input_Register_2,
  output R1___R2,
  output R1___R2_2,
  output [15:0] Output
);

  wire [15:0] adder_1_out, and_1_out, divider_1_out, multiplier_1_out, not_1_out, or_1_out, shifter_1_out,
       shifter_2_out, subtractor_1_out, xor_1_out;

  assign and_1_out = Input_Register_1 & Input_Register_2;  // AND_Gate and_1, 16 bits wide
  assign or_1_out = Input_Register_1 | Input_Register_2;  // OR_Gate or_1, 16 bits wide
  assign xor_1_out = Input_Register_1 ^ Input_Register_2;  // XOR_Gate xor_1, 16 bits wide
  assign not_1_out = ~Input_Register_1;  // NOT_Gate not_1, 16 bits wide
  Shifter #(.width(16)) shifter_1 (.in(Input_Register_1), .\dist (Input_Register_2[3:0]), .out(shifter_1_out));
  Shifter #(.width(16), .shift("lr")) shifter_2 (
    .in(Input_Register_1), .\dist (Input_Register_2[3:0]), .out(shifter_2_out));
  Adder #(.width(16)) adder_1 (.a(Input_Register_1), .b(Input_Register_2), .out(adder_1_out));  // open: cin, cout
  Subtractor #(.width(16)) subtractor_1 (
    .a(Input_Register_1), .b(Input_Register_2), .out(subtractor_1_out));  // open: bin, bout
  Multiplier #(.width(16)) multiplier_1 (
    .a(Input_Register_1), .b(Input_Register_2), .out(multiplier_1_out));  // open: cin, cout
  Divider #(.width(16)) divider_1 (
    .a(Input_Register_1), .b(Input_Register_2), .out(divider_1_out));  // open: upper, rem
  Comparator #(.width(16), .mode("unsigned")) comparator_1 (
    .a(Input_Register_1), .b(Input_Register_2), .gt(R1___R2), .eq(R1___R2_2));  // open: lt
  Multiplexer #(.select(4), .width(16), .enable("false")) multiplexer_1 (
    .in0({16{1'b0}}), .in1(and_1_out), .in2(or_1_out), .in3(xor_1_out), .in4(not_1_out), .in5(shifter_1_out),
    .in6(shifter_2_out), .in7(adder_1_out), .in8(subtractor_1_out), .in9(multiplier_1_out),
    .in10(divider_1_out), .in11({16{1'b0}}), .in12({16{1'b0}}), .in13({16{1'b0}}), .in14({16{1'b0}}),
    .in15({16{1'b0}}), .out(Output), .sel(Operation_Code));
endmodule

module Registers (
  input  Enable_Write,
  input  [2:0] RW_Select,
  input  [2:0] R1_Select,
  input  [2:0] R2_Select,
  input  [15:0] Data_In,
  input  Clock,
  output [15:0] R1_Out,
  output [15:0] R2_Out
);

  wire demultiplexer_1_out0, demultiplexer_1_out1, demultiplexer_1_out2, demultiplexer_1_out3,
       demultiplexer_1_out4, demultiplexer_1_out5, demultiplexer_1_out6, demultiplexer_1_out7;
  wire [15:0] register_1_q, register_2_q, register_3_q, register_4_q, register_5_q, register_6_q,
       register_7_q, register_8_q;

  Demultiplexer #(.select(3), .enable("false")) demultiplexer_1 (
    .out0(demultiplexer_1_out0), .out1(demultiplexer_1_out1), .out2(demultiplexer_1_out2),
    .out3(demultiplexer_1_out3), .out4(demultiplexer_1_out4), .out5(demultiplexer_1_out5),
    .out6(demultiplexer_1_out6), .out7(demultiplexer_1_out7), .in(Enable_Write), .sel(RW_Select));
  Register #(.width(16)) register_1 (
    .D(Data_In), .en(demultiplexer_1_out1), .Q(register_1_q), .clk(Clock));  // open: clr
  Register #(.width(16)) register_2 (
    .D(Data_In), .en(demultiplexer_1_out0), .Q(register_2_q), .clk(Clock));  // open: clr
  Register #(.width(16)) register_3 (
    .D(Data_In), .en(demultiplexer_1_out3), .Q(register_3_q), .clk(Clock));  // open: clr
  Register #(.width(16)) register_4 (
    .D(Data_In), .en(demultiplexer_1_out2), .Q(register_4_q), .clk(Clock));  // open: clr
  Register #(.width(16)) register_5 (
    .D(Data_In), .en(demultiplexer_1_out5), .Q(register_5_q), .clk(Clock));  // open: clr
  Register #(.width(16)) register_6 (
    .D(Data_In), .en(demultiplexer_1_out4), .Q(register_6_q), .clk(Clock));  // open: clr
  Register #(.width(16)) register_7 (
    .D(Data_In), .en(demultiplexer_1_out7), .Q(register_7_q), .clk(Clock));  // open: clr
  Register #(.width(16)) register_8 (
    .D(Data_In), .en(demultiplexer_1_out6), .Q(register_8_q), .clk(Clock));  // open: clr
  Multiplexer #(.select(3), .width(16), .enable("false")) multiplexer_1 (
    .in0(register_2_q), .in1(register_1_q), .in2(register_4_q), .in3(register_3_q), .in4(register_6_q),
    .in5(register_5_q), .in6(register_8_q), .in7(register_7_q), .out(R1_Out), .sel(R1_Select));
  Multiplexer #(.select(3), .width(16), .enable("false")) multiplexer_2 (
    .in0(register_2_q), .in1(register_1_q), .in2(register_4_q), .in3(register_3_q), .in4(register_6_q),
    .in5(register_5_q), .in6(register_8_q), .in7(register_7_q), .out(R2_Out), .sel(R2_Select));
endmodule

module Control (
  input  [15:0] IR_Output,
  input  Clock,
  input  R1___R2,
  input  R1___R2_2,
  output [2:0] R2_Select,
  output [2:0] R1_Select,
  output [2:0] RW_Select,
  output [3:0] Op_Code,
  output IM_Load,
  output Reg_Write,
  output PC_Load,
  output Reg_Select,
  output IR_Load,
  output Output,
  output PC_Select
);

  wire and_1_out, and_2_out, and_3_out, and_4_out, and_5_out, and_6_out, and_7_out, multiplexer_5_out,
       nand_1_out, not_1_out, not_2_out, not_3_out, not_4_out, not_5_out, not_6_out, not_7_out, not_8_out,
       not_9_out, or_1_out, or_2_out, or_3_out;
  wire [1:0] adder_1_out, phase;

  and and_1 (and_1_out, or_1_out, not_1_out);
  or or_1 (or_1_out, IR_Output[11], IR_Output[12], IR_Output[13], IR_Output[14]);
  not not_1 (not_1_out, IR_Output[15]);
  and and_2 (and_2_out, IR_Output[11], IR_Output[12], not_2_out, IR_Output[15]);
  not not_2 (not_2_out, IR_Output[13]);
  or or_2 (or_2_out, and_1_out, and_2_out);
  nand nand_1 (nand_1_out, IR_Output[11], IR_Output[12], not_3_out, IR_Output[14], IR_Output[15]);
  not not_3 (not_3_out, IR_Output[13]);
  Multiplexer #(.select(2), .enable("false")) multiplexer_1 (
    .in0(1'b0), .in1(1'b0), .in2(or_2_out), .in3(1'b0), .out(Reg_Write), .sel(phase));
  Multiplexer #(.select(2), .enable("false")) multiplexer_2 (
    .in0(1'b0), .in1(1'b0), .in2(nand_1_out), .in3(1'b0), .out(Reg_Select), .sel(phase));
  Multiplexer #(.select(2), .enable("false")) multiplexer_3 (
    .in0(1'b1), .in1(1'b0), .in2(1'b0), .in3(1'b0), .out(IR_Load), .sel(phase));
  and and_3 (and_3_out, IR_Output[14], IR_Output[15]);
  Multiplexer #(.select(2), .enable("false")) multiplexer_4 (
    .in0(1'b1), .in1(and_3_out), .in2(1'b0), .in3(1'b0), .out(PC_Select), .sel(phase));
  and and_4 (and_4_out, IR_Output[15], IR_Output[14], not_4_out, or_3_out);
  not not_4 (not_4_out, IR_Output[12]);
  Register #(.width(2)) u_Phase (.D(adder_1_out), .Q(phase), .clk(Clock), .clr(and_5_out));  // open: en
  and and_5 (and_5_out, phase[1], phase[0]);
  and and_6 (and_6_out, IR_Output[14], IR_Output[15]);
  and and_7 (and_7_out, IR_Output[14], IR_Output[15]);
  not not_5 (not_5_out, IR_Output[13]);
  or or_3 (or_3_out, not_5_out, multiplexer_5_out);
  Multiplexer #(.enable("false")) multiplexer_5 (
    .in0(R1___R2), .in1(R1___R2_2), .out(multiplexer_5_out), .sel(IR_Output[11]));
  not not_6 (not_6_out, IR_Output[11]);
  not not_7 (not_7_out, IR_Output[12]);
  and and_8 (Output, phase[1], not_6_out, not_7_out, not_8_out, not_9_out, IR_Output[15]);
  not not_8 (not_8_out, IR_Output[13]);
  not not_9 (not_9_out, IR_Output[14]);
  Multiplexer #(.select(2), .enable("false")) multiplexer_6 (
    .in0(1'b0), .in1(and_6_out), .in2(1'b0), .in3(1'b0), .out(IM_Load), .sel(phase));
  Multiplexer #(.select(2), .enable("false")) multiplexer_7 (
    .in0(1'b1), .in1(and_7_out), .in2(and_4_out), .in3(1'b0), .out(PC_Load), .sel(phase));
  Adder #(.width(2)) adder_1 (.a(phase), .b(2'b01), .out(adder_1_out));  // open: cin, cout

  assign Op_Code = IR_Output[14:11];
  assign R1_Select = IR_Output[7:5];
  assign R2_Select = IR_Output[2:0];
  assign RW_Select = IR_Output[10:8];

  // Other names for the same wires on the sheet: opbit4 = IR_Output[15]; opbit0 = IR_Output[11];
  //   opbit1 = IR_Output[12]; opbit2 = IR_Output[13]; opbit3 = IR_Output[14]
endmodule
