// Logisim project i08.circ as structural Verilog: 6 circuits, main circuit ALU
module main (
);

  wire clock_1_out, de_clocker_1_phase_2, i08_1_ram_write;
  wire [7:0] i08_1_r0_out, i08_1_ram_address, i08_1_ram_dbus, ram_1_data;

  RAM #(.bus("separate")) ram_1 (
    .addr(i08_1_ram_address), .din(i08_1_ram_dbus), .data(ram_1_data), .str(i08_1_ram_write),
    .clk(clock_1_out));  // open: sel, ld, clr
  Clock clock_1 (.out(clock_1_out));
  Hex_Digit_Display hex_digit_display_1 (.value(i08_1_r0_out[7:4]));  // open: dp
  i08 i08_1 (
    .RAM_Address(i08_1_ram_address), .Data_In(ram_1_data), .RAM_Write(i08_1_ram_write),
    .RAM_dbus(i08_1_ram_dbus), .Clock(clock_1_out), .R0_Out(i08_1_r0_out));
  Hex_Digit_Display hex_digit_display_2 (.value(i08_1_r0_out[3:0]));  // open: dp
  De_clocker de_clocker_1 (.Clock(clock_1_out), .Phase_2(de_clocker_1_phase_2));
  TTY tty_1 (.data(i08_1_r0_out[6:0]), .clk(de_clocker_1_phase_2));  // open: we, clr
endmodule

module i08 (
  input  [7:0] Data_In,
  input  Clock,
  output [7:0] RAM_Address,
  output RAM_Write,
  output [7:0] R0_Out,
  output [7:0] RAM_dbus
);

  wire alu_1_zero, imload, irload, pcload, pcsel, rdwrite;
  wire [1:0] addsel, aluop, rdin, rdsel, rssel;
  wire [7:0] adder_1_out, alu_1_result, Immed_q, IR_q, multiplexer_2_out, multiplexer_3_out, PC_q, sbus;

  Multiplexer #(.select(2), .width(8), .enable("false")) multiplexer_1 (
    .in0(PC_q), .in1(Immed_q), .in2(sbus), .in3(RAM_dbus), .out(RAM_Address), .sel(addsel));
  Register Immed (.D(Data_In), .en(imload), .Q(Immed_q), .clk(Clock));  // open: clr
  Register IR (.D(Data_In), .en(irload), .Q(IR_q), .clk(Clock));  // open: clr
  Control_Logic control_logic_1 (
    .IR_Load(irload), .RS_Select(rssel), .RD_Select(rdsel), .Aluop(aluop), .IM_Load(imload),
    .PC_Load(pcload), .RAM_Write(RAM_Write), .PC_Sel(pcsel), .Reg_Select(rdin), .RD_Write(rdwrite),
    .Address_Select(addsel), .IR_Input(IR_q), .Zero(alu_1_zero), .Clock(Clock));
  Multiplexer #(.width(8), .enable("false")) multiplexer_2 (
    .in0(Immed_q), .in1(adder_1_out), .out(multiplexer_2_out), .sel(pcsel));
  Multiplexer #(.select(2), .width(8), .enable("false")) multiplexer_3 (
    .in0(Immed_q), .in1(sbus), .in2(Data_In), .in3(alu_1_result), .out(multiplexer_3_out), .sel(rdin));
  Register PC (.D(multiplexer_2_out), .en(pcload), .Q(PC_q), .clk(Clock));  // open: clr
  Regs regs_1 (
    .Write_RD(rdwrite), .Data(multiplexer_3_out), .D_Register(RAM_dbus), .S_Register(sbus),
    .RD_Select(rdsel), .RS_Select(rssel), .Clock(Clock), .R0_Out(R0_Out));
  Adder adder_1 (.a(PC_q), .b(8'h1), .out(adder_1_out));  // open: cin, cout
  ALU alu_1 (
    .Register_D(RAM_dbus), .Register_S(sbus), .Result(alu_1_result), .Zero(alu_1_zero), .OP_Code(aluop));  // open: Carry

  // Other names for the same wires on the sheet: clk = Clock; dbus[7:0] = RAM_dbus; ramwrite = RAM_Write
endmodule

module ALU (
  input  [1:0] OP_Code,
  input  [7:0] Register_D,
  input  [7:0] Register_S,
  output [7:0] Result,
  output Carry,
  output Zero
);

  wire [7:0] adder_1_out, and_1_out, not_1_out, or_1_out, subtractor_1_out;

  assign and_1_out = Register_D & Register_S;  // AND_Gate and_1, 8 bits wide
  assign or_1_out = Register_D | Register_S;  // OR_Gate or_1, 8 bits wide
  Adder adder_1 (.a(Register_D), .b(Register_S), .out(adder_1_out), .cout(Carry));  // open: cin
  Subtractor subtractor_1 (.a(Register_D), .b(Register_S), .out(subtractor_1_out));  // open: bin, bout
  Multiplexer #(.select(2), .width(8), .enable("false")) multiplexer_1 (
    .in0(and_1_out), .in1(or_1_out), .in2(adder_1_out), .in3(subtractor_1_out), .out(Result), .sel(OP_Code));
  assign not_1_out = ~Result;  // NOT_Gate not_1, 8 bits wide
  and and_2 (Zero, not_1_out[0], not_1_out[1], not_1_out[2], not_1_out[3], not_1_out[4], not_1_out[5], not_1_out[6], not_1_out[7]);

  // Notes on the sheet:
  //   Operations: 00 AND; 01 OR; 10 ADD; 11 SUB
endmodule

module Regs (
  input  [1:0] RD_Select,
  input  [1:0] RS_Select,
  input  Write_RD,
  input  [7:0] Data,
  input  Clock,
  output [7:0] R0_Out,
  output [7:0] D_Register,
  output [7:0] S_Register
);

  wire demultiplexer_2_out0, demultiplexer_2_out1, demultiplexer_2_out2, demultiplexer_2_out3;
  wire [7:0] demultiplexer_1_out0, demultiplexer_1_out1, demultiplexer_1_out2, demultiplexer_1_out3,
       register_2_q, register_3_q, register_4_q;

  Demultiplexer #(.select(2), .width(8)) demultiplexer_1 (
    .out0(demultiplexer_1_out0), .out1(demultiplexer_1_out1), .out2(demultiplexer_1_out2),
    .out3(demultiplexer_1_out3), .in(Data), .sel(RD_Select), .en(Write_RD));
  Demultiplexer #(.select(2), .enable("false")) demultiplexer_2 (
    .out0(demultiplexer_2_out0), .out1(demultiplexer_2_out1), .out2(demultiplexer_2_out2),
    .out3(demultiplexer_2_out3), .in(Write_RD), .sel(RD_Select));
  Register register_1 (.D(demultiplexer_1_out0), .en(demultiplexer_2_out0), .Q(R0_Out), .clk(Clock));  // open: clr
  Register register_2 (
    .D(demultiplexer_1_out1), .en(demultiplexer_2_out1), .Q(register_2_q), .clk(Clock));  // open: clr
  Register register_3 (
    .D(demultiplexer_1_out2), .en(demultiplexer_2_out2), .Q(register_3_q), .clk(Clock));  // open: clr
  Register register_4 (
    .D(demultiplexer_1_out3), .en(demultiplexer_2_out3), .Q(register_4_q), .clk(Clock));  // open: clr
  Multiplexer #(.select(2), .width(8), .enable("false")) multiplexer_1 (
    .in0(R0_Out), .in1(register_2_q), .in2(register_3_q), .in3(register_4_q), .out(D_Register),
    .sel(RD_Select));
  Multiplexer #(.select(2), .width(8), .enable("false")) multiplexer_2 (
    .in0(R0_Out), .in1(register_2_q), .in2(register_3_q), .in3(register_4_q), .out(S_Register),
    .sel(RS_Select));
endmodule

module Control_Logic (
  input  [7:0] IR_Input,
  input  Clock,
  input  Zero,
  output IR_Load,
  output [1:0] RS_Select,
  output [1:0] RD_Select,
  output [1:0] Aluop,
  output IM_Load,
  output PC_Load,
  output RAM_Write,
  output PC_Sel,
  output [1:0] Reg_Select,
  output RD_Write,
  output [1:0] Address_Select
);

  wire and_1_out, and_2_out, and_3_out, and_4_out, multiplexer_1_out, multiplexer_11_out, not_1_out,
       not_2_out, not_3_out, or_1_out;
  wire [1:0] adder_1_out, multiplexer_6_out, multiplexer_7_out, phase;

  Multiplexer #(.select(2), .enable("false")) multiplexer_1 (
    .in0(Zero), .in1(not_1_out), .in2(Zero), .in3(Zero), .out(multiplexer_1_out), .sel(IR_Input[5:4]));
  not not_1 (not_1_out, Zero);
  not not_2 (not_2_out, IR_Input[6]);
  and and_1 (and_1_out, IR_Input[7], not_2_out, multiplexer_1_out);
  or or_1 (or_1_out, and_1_out, and_2_out);
  and and_2 (and_2_out, IR_Input[7], IR_Input[6], IR_Input[5], IR_Input[4]);
  Multiplexer #(.select(2), .enable("false")) multiplexer_2 (
    .in0(1'b1), .in1(1'b0), .in2(1'b0), .in3(1'b0), .out(IR_Load), .sel(phase));
  Multiplexer #(.select(2), .enable("false")) multiplexer_3 (
    .in0(1'b0), .in1(IR_Input[7]), .in2(1'b0), .in3(1'b0), .out(IM_Load), .sel(phase));
  Multiplexer #(.select(2), .enable("false")) multiplexer_4 (
    .in0(1'b1), .in1(IR_Input[7]), .in2(or_1_out), .in3(1'b0), .out(PC_Load), .sel(phase));
  Multiplexer #(.select(2), .enable("false")) multiplexer_5 (
    .in0(1'b1), .in1(1'b1), .in2(1'b0), .in3(1'b0), .out(PC_Sel), .sel(phase));
  Multiplexer #(.select(4), .width(2), .enable("false")) multiplexer_6 (
    .in0(2'b11), .in1(2'b11), .in2(2'b11), .in3(2'b11), .in6(2'b01), .in7(2'b00), .in8(2'b00), .in9(2'b00),
    .in10(2'b00), .in11(2'b00), .in12(2'b00), .in13(2'b00), .in14(2'b00), .in15(2'b00),
    .out(multiplexer_6_out), .sel(IR_Input[7:4]));  // open: in4, in5
  Multiplexer #(.select(4), .width(2), .enable("false")) multiplexer_7 (
    .in0(2'b00), .in1(2'b00), .in2(2'b00), .in3(2'b00), .in4(2'b10), .in5(2'b10), .in6(2'b00), .in7(2'b00),
    .in8(2'b00), .in9(2'b00), .in10(2'b00), .in11(2'b00), .in12(2'b00), .in13(2'b01), .in14(2'b01),
    .in15(2'b00), .out(multiplexer_7_out), .sel(IR_Input[7:4]));
  and and_3 (and_3_out, IR_Input[4], not_3_out, IR_Input[6]);
  not not_3 (not_3_out, IR_Input[5]);
  Multiplexer #(.select(2), .enable("false")) multiplexer_8 (
    .in0(1'b0), .in1(1'b0), .in2(and_3_out), .in3(1'b0), .out(RAM_Write), .sel(phase));
  Multiplexer #(.select(2), .width(2), .enable("false")) multiplexer_9 (
    .in0(2'b00), .in1(2'b00), .in2(multiplexer_6_out), .in3(2'b00), .out(Reg_Select), .sel(phase));
  Multiplexer #(.select(2), .width(2), .enable("false")) multiplexer_10 (
    .in0(2'b00), .in1(2'b00), .in2(multiplexer_7_out), .in3(2'b00), .out(Address_Select), .sel(phase));
  Multiplexer #(.select(4), .enable("false")) multiplexer_11 (
    .in0(1'b1), .in1(1'b1), .in2(1'b1), .in3(1'b1), .in4(1'b1), .in5(1'b0), .in6(1'b1), .in7(1'b0),
    .in8(1'b0), .in9(1'b0), .in10(1'b0), .in11(1'b0), .in12(1'b1), .in13(1'b0), .in14(1'b1), .in15(1'b0),
    .out(multiplexer_11_out), .sel(IR_Input[7:4]));
  Register #(.width(2)) u_Phase (.D(adder_1_out), .Q(phase), .clk(Clock), .clr(and_4_out));  // open: en
  and and_4 (and_4_out, phase[1], phase[0]);
  Multiplexer #(.select(2), .enable("false")) multiplexer_12 (
    .in0(1'b0), .in1(1'b0), .in2(multiplexer_11_out), .in3(1'b0), .out(RD_Write), .sel(phase));
  Adder #(.width(2)) adder_1 (.a(phase), .b(2'b01), .out(adder_1_out));  // open: cin, cout

  assign Aluop = IR_Input[5:4];
  assign RD_Select = IR_Input[3:2];
  assign RS_Select = IR_Input[1:0];

  // Other names for the same wires on the sheet: irbit4 = IR_Input[4]; op2[1:0] = IR_Input[5:4];
  //   op12[3:0] = IR_Input[7:4]; irbit5 = IR_Input[5]; irbit6 = IR_Input[6]; op1[1:0] = IR_Input[7:6];
  //   irbit7 = IR_Input[7]
endmodule

module De_clocker (
  input  Clock,
  output Phase_2
);

  wire and_1_out;
  wire [0:0] Phase_q;
  wire [1:0] adder_1_out;

  Register #(.width(2)) Phase (.D(adder_1_out), .Q({Phase_2, Phase_q[0]}), .clk(Clock), .clr(and_1_out));  // open: en
  and and_1 (and_1_out, Phase_2, Phase_q[0]);
  Adder #(.width(2)) adder_1 (.a({Phase_2, Phase_q[0]}), .b(2'b01), .out(adder_1_out));  // open: cin, cout
endmodule
