// Logisim project m24.circ as structural Verilog: 4 circuits, main circuit m24 Setups
module m24_Setups (
  output [23:0] out_1
);

  wire clock_1_out, m24_internal_cpu_1_ram_write, undriven_2;
  wire [6:0] undriven;
  wire [15:0] m24_internal_cpu_1_ram_add_out;
  wire [19:0] m24_internal_cpu_1_rom_add_out;
  wire [20:0] demultiplexer_1_out0, demultiplexer_1_out1, demultiplexer_1_out2, demultiplexer_1_out3,
       demultiplexer_1_out4, demultiplexer_1_out5, demultiplexer_1_out6, demultiplexer_1_out7;
  wire [23:0] m24_internal_cpu_1_ram_data_out, ram_1_data, undriven_3, undriven_4;
  wire [31:0] rom_1_data;

  RAM #(.addrWidth(16), .dataWidth(24), .bus("separate")) ram_1 (
    .addr(m24_internal_cpu_1_ram_add_out), .din(m24_internal_cpu_1_ram_data_out), .data(ram_1_data),
    .str(m24_internal_cpu_1_ram_write), .clk(clock_1_out));  // open: sel, ld, clr
  ROM #(.addrWidth(20), .dataWidth(32)) rom_1 (.addr(m24_internal_cpu_1_rom_add_out), .data(rom_1_data));  // open: sel
  m24_internal_CPU m24_internal_cpu_1 (
    .RAM_ADD_OUT(m24_internal_cpu_1_ram_add_out), .RAM_DATA_IN(ram_1_data),
    .RAM_DATA_OUT(m24_internal_cpu_1_ram_data_out), .RAM_WRITE(m24_internal_cpu_1_ram_write),
    .ROM_ADD_OUT(m24_internal_cpu_1_rom_add_out), .PROGRAM_IN(rom_1_data), .OUTPUT(out_1), .Clock(clock_1_out));
  Clock clock_1 (.out(clock_1_out));
  TTY tty_1 (.data(undriven), .clk(undriven_2));  // open: we, clr
  DotMatrix #(.inputtype("row"), .matrixcols(8), .matrixrows(3), .persist(2)) dotmatrix_1 (
    .row0(undriven_4[7:0]), .row1(undriven_4[15:8]), .row2(undriven_4[23:16]));
  DotMatrix #(.inputtype("row"), .matrixcols(21), .matrixrows(8), .persist(64)) dotmatrix_2 (
    .row0(demultiplexer_1_out0), .row1(demultiplexer_1_out1), .row2(demultiplexer_1_out2),
    .row3(demultiplexer_1_out3), .row4(demultiplexer_1_out4), .row5(demultiplexer_1_out5),
    .row6(demultiplexer_1_out6), .row7(demultiplexer_1_out7));
  Demultiplexer #(.select(3), .width(21), .disabled(0), .enable("false")) demultiplexer_1 (
    .out0(demultiplexer_1_out0), .out1(demultiplexer_1_out1), .out2(demultiplexer_1_out2),
    .out3(demultiplexer_1_out3), .out4(demultiplexer_1_out4), .out5(demultiplexer_1_out5),
    .out6(demultiplexer_1_out6), .out7(demultiplexer_1_out7), .in(undriven_3[20:0]), .sel(undriven_3[23:21]));

  // Notes on the sheet:
  //   contents of rom_1 (hex, n*v repeats v):
  //   4c000001 4d000001 4e000000 1c600000 4b000000 40000000 4a400000 49c00000 50000003
  //   LED
  //   TTY
  //   HD
endmodule

module m24_internal_CPU (
  input  [31:0] PROGRAM_IN,
  input  [23:0] RAM_DATA_IN,
  input  Clock,
  output [19:0] ROM_ADD_OUT,
  output [15:0] RAM_ADD_OUT,
  output [23:0] RAM_DATA_OUT,
  output RAM_WRITE,
  output [23:0] OUTPUT
);

  wire m24_internal_alu_1_r1___r2, m24_internal_alu_1_r1___r2_2, multiplexer_2_out;
  wire [7:1] rom_1_data;
  wire [19:0] adder_1_out, multiplexer_1_out;
  wire [23:0] m24_internal_alu_1_output_data, m24_internal_reg_1_r2_data_out, multiplexer_4_out;

  Multiplexer #(.width(20), .enable("false")) multiplexer_1 (
    .in0(adder_1_out), .in1(PROGRAM_IN[19:0]), .out(multiplexer_1_out), .sel(multiplexer_2_out));
  Register #(.width(20)) register_1 (.D(multiplexer_1_out), .Q(ROM_ADD_OUT), .clk(Clock));  // open: en, clr
  Adder #(.width(20)) adder_1 (.a(ROM_ADD_OUT), .b(20'h1), .out(adder_1_out));  // open: cin, cout
  Multiplexer #(.select(2), .enable("false")) multiplexer_2 (
    .in0(1'b0), .in1(1'b1), .in2(m24_internal_alu_1_r1___r2_2), .in3(m24_internal_alu_1_r1___r2),
    .out(multiplexer_2_out), .sel(rom_1_data[4:3]));
  ROM #(.addrWidth(6)) rom_1 (.addr(PROGRAM_IN[31:26]), .data({rom_1_data, RAM_WRITE}));  // open: sel
  Multiplexer #(.select(2), .width(24), .enable("false")) multiplexer_3 (
    .in0({24{1'b0}}), .in1(RAM_DATA_OUT), .in2(PROGRAM_IN[23:0]), .in3(RAM_DATA_IN), .out(OUTPUT),
    .sel(rom_1_data[2:1]));
  Multiplexer #(.select(2), .width(24), .enable("false")) multiplexer_4 (
    .in0(m24_internal_alu_1_output_data), .in1(PROGRAM_IN[23:0]), .in2(RAM_DATA_IN), .in3(RAM_DATA_OUT),
    .out(multiplexer_4_out), .sel(rom_1_data[6:5]));
  m24_internal_REG m24_internal_reg_1 (
    .Enable_Write(rom_1_data[7]), .Data_In(multiplexer_4_out), .Out_R1(PROGRAM_IN[23:22]),
    .R1_Data_Out(RAM_DATA_OUT), .Out_R2(PROGRAM_IN[21:20]), .R2_Data_Out(m24_internal_reg_1_r2_data_out),
    .Write_Reg(PROGRAM_IN[25:24]), .Clock(Clock));
  m24_internal_ALU m24_internal_alu_1 (
    .Input_Register_1(RAM_DATA_OUT), .Input_Register_2(m24_internal_reg_1_r2_data_out),
    .Output_Data(m24_internal_alu_1_output_data), .Op_Code(PROGRAM_IN[29:26]),
    .R1___R2(m24_internal_alu_1_r1___r2), .R1___R2_2(m24_internal_alu_1_r1___r2_2));

  assign RAM_ADD_OUT = PROGRAM_IN[15:0];

  // Notes on the sheet:
  //   ROM Address
  //   Microcode
  //   contents of rom_1 (hex, n*v repeats v):
  //   0 11*80 4*0 2 4 e0 a0 8 10 18 1 c0 6
endmodule

module m24_internal_ALU (
  input  [23:0] Input_Register_1,
  input  [3:0] Op_Code,
  input  [23:0] Input_Register_2,
  output R1___R2,
  output R1___R2_2,
  output [23:0] Output_Data
);

  wire [23:0] adder_1_out, and_1_out, divider_1_out, divider_1_rem, multiplier_1_out, not_1_out, or_1_out,
       shifter_1_out, shifter_2_out, subtractor_1_out, xor_1_out;

  assign and_1_out = Input_Register_1 & Input_Register_2;  // AND_Gate and_1, 24 bits wide
  assign or_1_out = Input_Register_1 | Input_Register_2;  // OR_Gate or_1, 24 bits wide
  assign xor_1_out = Input_Register_1 ^ Input_Register_2;  // XOR_Gate xor_1, 24 bits wide
  assign not_1_out = ~Input_Register_1;  // NOT_Gate not_1, 24 bits wide
  Shifter #(.width(24)) shifter_1 (.in(Input_Register_1), .\dist (Input_Register_2[4:0]), .out(shifter_1_out));
  Shifter #(.width(24), .shift("lr")) shifter_2 (
    .in(Input_Register_1), .\dist (Input_Register_2[4:0]), .out(shifter_2_out));
  Adder #(.width(24)) adder_1 (.a(Input_Register_1), .b(Input_Register_2), .out(adder_1_out));  // open: cin, cout
  Subtractor #(.width(24)) subtractor_1 (
    .a(Input_Register_1), .b(Input_Register_2), .out(subtractor_1_out));  // open: bin, bout
  Multiplier #(.width(24)) multiplier_1 (
    .a(Input_Register_1), .b(Input_Register_2), .out(multiplier_1_out));  // open: cin, cout
  Divider #(.width(24)) divider_1 (
    .a(Input_Register_1), .b(Input_Register_2), .out(divider_1_out), .rem(divider_1_rem));  // open: upper
  Comparator #(.width(24)) comparator_1 (
    .a(Input_Register_1), .b(Input_Register_2), .gt(R1___R2), .eq(R1___R2_2));  // open: lt
  Multiplexer #(.select(4), .width(24), .disabled(0), .enable("false")) multiplexer_1 (
    .in0({24{1'b0}}), .in1(and_1_out), .in2(or_1_out), .in3(xor_1_out), .in4(not_1_out), .in5(shifter_1_out),
    .in6(shifter_2_out), .in7(adder_1_out), .in8(subtractor_1_out), .in9(multiplier_1_out),
    .in10(divider_1_out), .in11(divider_1_rem), .in12({24{1'b0}}), .in13({24{1'b0}}), .in14({24{1'b0}}),
    .in15({24{1'b0}}), .out(Output_Data), .sel(Op_Code));
endmodule

module m24_internal_REG (
  input  [1:0] Write_Reg,
  input  [1:0] Out_R1,
  input  Enable_Write,
  input  [23:0] Data_In,
  input  [1:0] Out_R2,
  input  Clock,
  output [23:0] R1_Data_Out,
  output [23:0] R2_Data_Out
);

  wire demultiplexer_1_out0, demultiplexer_1_out1, demultiplexer_1_out2, demultiplexer_1_out3;
  wire [23:0] register_1_q, register_2_q, register_3_q, register_4_q;

  Demultiplexer #(.select(2), .disabled(0), .enable("false")) demultiplexer_1 (
    .out0(demultiplexer_1_out0), .out1(demultiplexer_1_out1), .out2(demultiplexer_1_out2),
    .out3(demultiplexer_1_out3), .in(Enable_Write), .sel(Write_Reg));
  Register #(.width(24)) register_1 (
    .D(Data_In), .en(demultiplexer_1_out2), .Q(register_1_q), .clk(Clock));  // open: clr
  Register #(.width(24)) register_2 (
    .D(Data_In), .en(demultiplexer_1_out3), .Q(register_2_q), .clk(Clock));  // open: clr
  Register #(.width(24)) register_3 (
    .D(Data_In), .en(demultiplexer_1_out0), .Q(register_3_q), .clk(Clock));  // open: clr
  Register #(.width(24)) register_4 (
    .D(Data_In), .en(demultiplexer_1_out1), .Q(register_4_q), .clk(Clock));  // open: clr
  Multiplexer #(.select(2), .width(24), .enable("false")) multiplexer_1 (
    .in0(register_3_q), .in1(register_4_q), .in2(register_1_q), .in3(register_2_q), .out(R1_Data_Out),
    .sel(Out_R1));
  Multiplexer #(.select(2), .width(24), .enable("false")) multiplexer_2 (
    .in0(register_3_q), .in1(register_4_q), .in2(register_1_q), .in3(register_2_q), .out(R2_Data_Out),
    .sel(Out_R2));
endmodule
